// Logisim project FinaleEierUhr.circ as structural Verilog: 7 circuits, main circuit main
module main (
  output out_1,
  output out_2,
  output out_3,
  output out_4,
  output out_5,
  output out_6
);

  wire Minuten_out, Sekunden_out, Start_out, Stop_out;
  wire [6:0] counter_1_out_6, counter_1_out_7, counter_1_out_8, counter_1_out_9;

  Button Sekunden (.out(Sekunden_out));
  Button Minuten (.out(Minuten_out));
  Button Start (.out(Start_out));
  Button Stop (.out(Stop_out));
  _7_Segment_Display u_7_segment_display_1 (
    .g(counter_1_out_9[0]), .f(counter_1_out_9[1]), .a(counter_1_out_9[2]), .b(counter_1_out_9[3]),
    .e(counter_1_out_9[4]), .d(counter_1_out_9[5]), .c(counter_1_out_9[6]));  // open: dp
  Counter counter_1 (
    .Sekunden(Sekunden_out), .Minuten(Minuten_out), .Start(Start_out), .Stop(Stop_out), .Alarm(out_1),
    .out_6(counter_1_out_6), .out_7(counter_1_out_7), .out_8(counter_1_out_8), .out_9(counter_1_out_9));
  _7_Segment_Display u_7_segment_display_2 (
    .g(counter_1_out_8[0]), .f(counter_1_out_8[1]), .a(counter_1_out_8[2]), .b(counter_1_out_8[3]),
    .e(counter_1_out_8[4]), .d(counter_1_out_8[5]), .c(counter_1_out_8[6]));  // open: dp
  _7_Segment_Display u_7_segment_display_3 (
    .g(counter_1_out_7[0]), .f(counter_1_out_7[1]), .a(counter_1_out_7[2]), .b(counter_1_out_7[3]),
    .e(counter_1_out_7[4]), .d(counter_1_out_7[5]), .c(counter_1_out_7[6]));  // open: dp
  _7_Segment_Display u_7_segment_display_4 (
    .g(counter_1_out_6[0]), .f(counter_1_out_6[1]), .a(counter_1_out_6[2]), .b(counter_1_out_6[3]),
    .e(counter_1_out_6[4]), .d(counter_1_out_6[5]), .c(counter_1_out_6[6]));  // open: dp

  assign out_2 = out_1;
  assign out_3 = out_1;
  assign out_4 = out_1;
  assign out_5 = out_1;
  assign out_6 = out_1;
endmodule

module Counter (
  input  Sekunden,
  input  Minuten,
  input  Start,
  input  Stop,
  output Alarm,
  output [6:0] out_6,
  output [6:0] out_7,
  output [6:0] out_8,
  output [6:0] out_9
);

  wire alarm_1_alarmreset, and_1_out, and_2_out, and_3_out, and_4_out, and_5_out, and_6_out, clock_1_out,
       counter_1_carry, counter_3_carry, counter_5_carry, counter_6_carry, counter_7_carry, d_ff_1_q,
       d_ff_2_q, d_ff_3_q, d_ff_4_q, d_ff_5_q, d_ff_6_q, eingangssynchronisierung_1_minuten_2,
       eingangssynchronisierung_1_reset_durch_stop, eingangssynchronisierung_1_sekunden_2,
       eingangssynchronisierung_1_up_down, or_1_out, taktgeber_1__1_sekunden_takt;
  wire [3:0] counter_1_q, counter_2_q, counter_3_q, counter_4_q, counter_5_q, counter_6_q, counter_7_q,
       counter_8_q, multiplexer_1_out, multiplexer_2_out, multiplexer_3_out, multiplexer_4_out,
       multiplexer_5_out, multiplexer_6_out, multiplexer_7_out, multiplexer_8_out;

  Eingangssynchronisierung eingangssynchronisierung_1 (
    .Sekunden(Sekunden), .Minuten(Minuten), .Start(Start), .Stop(Stop),
    .Sekunden_2(eingangssynchronisierung_1_sekunden_2), .Minuten_2(eingangssynchronisierung_1_minuten_2),
    .Up_Down(eingangssynchronisierung_1_up_down),
    .Reset_durch_Stop(eingangssynchronisierung_1_reset_durch_stop));
  Multiplex_Anzeige multiplex_anzeige_1 (
    .in_1(multiplexer_1_out), .in_2(multiplexer_2_out), .in_3(multiplexer_3_out), .in_4(multiplexer_8_out),
    .out_5(out_6), .out_6(out_7), .out_7(out_8), .out_8(out_9));
  or or_1 (or_1_out, eingangssynchronisierung_1_reset_durch_stop, alarm_1_alarmreset);
  Clock clock_1 (.out(clock_1_out));
  Counter_part #(.width(4), .max('ha)) counter_1 (
    .load(and_1_out), .count(eingangssynchronisierung_1_sekunden_2), .Q(counter_1_q),
    .carry(counter_1_carry), .clk(clock_1_out), .clr(or_1_out));  // open: D
  Counter_part #(.width(4), .max('h5)) counter_2 (
    .count(and_1_out), .Q(counter_2_q), .clk(clock_1_out), .clr(or_1_out));  // open: load, D, carry
  Counter_part #(.width(4), .max('ha)) counter_3 (
    .load(and_3_out), .count(eingangssynchronisierung_1_minuten_2), .Q(counter_3_q), .carry(counter_3_carry),
    .clk(clock_1_out), .clr(or_1_out));  // open: D
  Counter_part #(.width(4), .max('h5)) counter_4 (
    .count(and_3_out), .Q(counter_4_q), .clk(clock_1_out), .clr(or_1_out));  // open: load, D, carry
  Multiplexer #(.width(4)) multiplexer_1 (
    .in0(counter_1_q), .in1(counter_5_q), .out(multiplexer_1_out), .sel(eingangssynchronisierung_1_up_down));  // open: en
  D_Flip_Flop d_ff_1 (.clk(clock_1_out), .D(counter_1_carry), .Q(d_ff_1_q), .reset(or_1_out));  // open: Qn, preset, en
  D_Flip_Flop d_ff_2 (.clk(clock_1_out), .D(counter_3_carry), .Q(d_ff_2_q), .reset(or_1_out));  // open: Qn, preset, en
  D_Flip_Flop d_ff_3 (
    .clk(clock_1_out), .D(eingangssynchronisierung_1_up_down), .Q(d_ff_3_q), .reset(or_1_out));  // open: Qn, preset, en
  and and_1 (and_1_out, ~d_ff_1_q, counter_1_carry);  // AND_Gate
  Multiplexer #(.width(4)) multiplexer_2 (
    .in0(counter_2_q), .in1(counter_6_q), .out(multiplexer_2_out), .sel(eingangssynchronisierung_1_up_down));  // open: en
  and and_2 (and_2_out, ~d_ff_3_q, eingangssynchronisierung_1_up_down);  // AND_Gate
  and and_3 (and_3_out, ~d_ff_2_q, counter_3_carry);  // AND_Gate
  Multiplexer #(.width(4)) multiplexer_3 (
    .in0(counter_3_q), .in1(counter_7_q), .out(multiplexer_3_out), .sel(eingangssynchronisierung_1_up_down));  // open: en
  Multiplexer #(.width(4)) multiplexer_4 (
    .in0(counter_5_q), .in1(counter_1_q), .out(multiplexer_4_out), .sel(and_2_out));  // open: en
  Taktgeber taktgeber_1 (._1_Sekunden_Takt(taktgeber_1__1_sekunden_takt));
  Multiplexer #(.width(4)) multiplexer_5 (
    .in0(counter_6_q), .in1(counter_2_q), .out(multiplexer_5_out), .sel(and_2_out));  // open: en
  Multiplexer #(.width(4)) multiplexer_6 (
    .in0(counter_7_q), .in1(counter_3_q), .out(multiplexer_6_out), .sel(and_2_out));  // open: en
  Multiplexer #(.width(4)) multiplexer_7 (
    .in0(counter_8_q), .in1(counter_4_q), .out(multiplexer_7_out), .sel(and_2_out));  // open: en
  Counter_part #(.width(4), .max('h9)) counter_5 (
    .load(eingangssynchronisierung_1_up_down), .D(multiplexer_4_out), .count(taktgeber_1__1_sekunden_takt),
    .Q(counter_5_q), .carry(counter_5_carry), .clk(clock_1_out), .clr(or_1_out));
  Counter_part #(.width(4), .max('h5)) counter_6 (
    .load(eingangssynchronisierung_1_up_down), .D(multiplexer_5_out), .count(and_4_out), .Q(counter_6_q),
    .carry(counter_6_carry), .clk(clock_1_out));  // open: clr
  Counter_part #(.width(4), .max('h9)) counter_7 (
    .load(eingangssynchronisierung_1_up_down), .D(multiplexer_6_out), .count(and_5_out), .Q(counter_7_q),
    .carry(counter_7_carry), .clk(clock_1_out), .clr(or_1_out));
  Counter_part #(.width(4), .max('h5)) counter_8 (
    .load(eingangssynchronisierung_1_up_down), .D(multiplexer_7_out), .count(and_6_out), .Q(counter_8_q),
    .clk(clock_1_out), .clr(or_1_out));  // open: carry
  Multiplexer #(.width(4)) multiplexer_8 (
    .in0(counter_4_q), .in1(counter_8_q), .out(multiplexer_8_out), .sel(eingangssynchronisierung_1_up_down));  // open: en
  D_Flip_Flop d_ff_4 (.clk(clock_1_out), .D(counter_5_carry), .Q(d_ff_4_q), .reset(or_1_out));  // open: Qn, preset, en
  D_Flip_Flop d_ff_5 (.clk(clock_1_out), .D(counter_6_carry), .Q(d_ff_5_q), .reset(or_1_out));  // open: Qn, preset, en
  D_Flip_Flop d_ff_6 (.clk(clock_1_out), .D(counter_7_carry), .Q(d_ff_6_q), .reset(or_1_out));  // open: Qn, preset, en
  and and_4 (and_4_out, ~d_ff_4_q, counter_5_carry);  // AND_Gate
  and and_5 (and_5_out, ~d_ff_5_q, counter_6_carry);  // AND_Gate
  and and_6 (and_6_out, ~d_ff_6_q, counter_7_carry);  // AND_Gate
  Alarm alarm_1 (
    .in_1(multiplexer_1_out), .in_2(multiplexer_2_out), .in_3(multiplexer_3_out), .in_4(multiplexer_8_out),
    .Stop(eingangssynchronisierung_1_reset_durch_stop), .Up_Down(eingangssynchronisierung_1_up_down),
    .AlarmReset(alarm_1_alarmreset), .Alarmsignal(Alarm));
endmodule

module Alarm (
  input  [3:0] in_1,
  input  [3:0] in_2,
  input  [3:0] in_3,
  input  [3:0] in_4,
  input  Stop,
  input  Up_Down,
  output AlarmReset,
  output Alarmsignal
);

  wire and_3_out, clock_1_out, d_ff_1_qn, taktgeber_1__1_sekunden_takt;
  wire [3:0] and_1_out;

  assign and_1_out = ~in_1 & ~in_2 & ~in_3 & ~in_4;  // AND_Gate and_1, 4 bits wide
  Taktgeber taktgeber_1 (._1_Sekunden_Takt(taktgeber_1__1_sekunden_takt));
  and and_2 (AlarmReset, and_1_out[0], and_1_out[1], and_1_out[2], and_1_out[3], Up_Down);
  and and_3 (and_3_out, AlarmReset, taktgeber_1__1_sekunden_takt);
  Clock clock_1 (.out(clock_1_out));
  D_Flip_Flop d_ff_1 (
    .clk(clock_1_out), .D(d_ff_1_qn), .Q(Alarmsignal), .Qn(d_ff_1_qn), .en(and_3_out), .reset(Stop));  // open: preset
endmodule

module Multiplex_Anzeige (
  input  [3:0] in_1,
  input  [3:0] in_2,
  input  [3:0] in_3,
  input  [3:0] in_4,
  output [6:0] out_5,
  output [6:0] out_6,
  output [6:0] out_7,
  output [6:0] out_8
);

  wire clock_1_out;
  wire [1:0] counter_1_q;
  wire [3:0] multiplexer_1_out;
  wire [6:0] bcd_codierer_1_a;

  Clock clock_1 (.out(clock_1_out));
  Counter_part #(.width(2), .max('h3)) counter_1 (
    .Q(counter_1_q), .clk(clock_1_out));  // open: load, D, count, carry, clr
  Multiplexer #(.select(2), .width(4)) multiplexer_1 (
    .in0(in_1), .in1(in_2), .in2(in_3), .in3(in_4), .out(multiplexer_1_out), .sel(counter_1_q));  // open: en
  BCD_Codierer bcd_codierer_1 (
    .E3(multiplexer_1_out[3]), .E2(multiplexer_1_out[2]), .E1(multiplexer_1_out[1]),
    .E0(multiplexer_1_out[0]), .a(bcd_codierer_1_a[0]), .b(bcd_codierer_1_a[1]), .c(bcd_codierer_1_a[2]),
    .d(bcd_codierer_1_a[3]), .e(bcd_codierer_1_a[4]), .f(bcd_codierer_1_a[5]), .g(bcd_codierer_1_a[6]));
  Demultiplexer #(.select(2), .width(7)) demultiplexer_1 (
    .out0(out_5), .out1(out_6), .out2(out_7), .out3(out_8), .in(bcd_codierer_1_a), .sel(counter_1_q));  // open: en
endmodule

module Taktgeber (
  output _1_Sekunden_Takt
);

  wire clock_1_out;

  Clock clock_1 (.out(clock_1_out));
  Counter_part #(.width(9), .max('h1f3)) counter_1 (
    .carry(_1_Sekunden_Takt), .clk(clock_1_out));  // open: load, D, count, Q, clr
endmodule

module Eingangssynchronisierung (
  input  Sekunden,
  input  Minuten,
  input  Start,
  input  Stop,
  output Sekunden_2,
  output Minuten_2,
  output Up_Down,
  output Reset_durch_Stop
);

  wire clock_1_out, d_ff_1_q, d_ff_2_q;

  Clock clock_1 (.out(clock_1_out));
  D_Flip_Flop d_ff_1 (.clk(clock_1_out), .D(Sekunden), .Q(d_ff_1_q));  // open: Qn, preset, en, reset
  D_Flip_Flop d_ff_2 (.clk(clock_1_out), .D(Minuten), .Q(d_ff_2_q));  // open: Qn, preset, en, reset
  D_Flip_Flop d_ff_3 (
    .clk(clock_1_out), .D(1'b1), .Q(Up_Down), .en(Start), .reset(Reset_durch_Stop));  // open: Qn, preset
  D_Flip_Flop d_ff_4 (.clk(clock_1_out), .D(Stop), .Q(Reset_durch_Stop));  // open: Qn, preset, en, reset
  and and_1 (Sekunden_2, Sekunden, ~d_ff_1_q);  // AND_Gate
  and and_2 (Minuten_2, Minuten, ~d_ff_2_q);  // AND_Gate
endmodule

module BCD_Codierer (
  input  E3,
  input  E2,
  input  E1,
  input  E0,
  output a,
  output b,
  output c,
  output d,
  output e,
  output f,
  output g
);

  wire and_1_out, and_2_out, and_3_out, and_4_out, and_5_out, and_6_out, and_7_out, and_8_out, and_9_out,
       and_10_out, and_11_out, and_12_out, and_13_out, and_14_out, and_15_out, and_16_out, and_17_out,
       and_18_out, and_19_out, and_20_out, and_21_out, and_22_out, and_23_out, not_1_out, not_2_out,
       not_3_out, not_4_out, not_5_out, not_6_out, not_7_out, not_8_out, not_9_out, not_10_out, not_11_out,
       not_12_out, not_13_out, not_14_out, not_15_out, not_16_out, not_17_out, not_18_out, not_19_out,
       not_20_out, not_21_out, not_22_out, not_23_out, not_24_out, not_25_out, not_26_out, not_27_out,
       not_28_out, not_29_out;

  not not_1 (not_1_out, E2);
  and and_1 (and_1_out, not_1_out, E1);
  and and_2 (and_2_out, E2, not_2_out);
  not not_2 (not_2_out, E1);
  and and_3 (and_3_out, E2, not_3_out);
  not not_3 (not_3_out, E0);
  not not_4 (not_4_out, E1);
  and and_4 (and_4_out, not_4_out, not_5_out);
  not not_5 (not_5_out, E0);
  and and_5 (and_5_out, E2, not_6_out);
  not not_6 (not_6_out, E1);
  and and_6 (and_6_out, E2, not_7_out);
  not not_7 (not_7_out, E0);
  not not_8 (not_8_out, E2);
  and and_7 (and_7_out, not_8_out, not_9_out);
  not not_9 (not_9_out, E0);
  and and_8 (and_8_out, E2, E0);
  not not_10 (not_10_out, E3);
  and and_9 (and_9_out, not_10_out, not_11_out);
  not not_11 (not_11_out, E2);
  not not_12 (not_12_out, E3);
  not not_13 (not_13_out, E1);
  and and_10 (and_10_out, not_12_out, not_13_out, not_14_out);
  not not_14 (not_14_out, E0);
  not not_15 (not_15_out, E2);
  and and_11 (and_11_out, not_15_out, not_16_out);
  not not_16 (not_16_out, E1);
  not not_17 (not_17_out, E3);
  and and_12 (and_12_out, not_17_out, E1, E0);
  not not_18 (not_18_out, E2);
  and and_13 (and_13_out, not_18_out, not_19_out);
  not not_19 (not_19_out, E0);
  and and_14 (and_14_out, E1, not_20_out);
  not not_20 (not_20_out, E0);
  and and_15 (and_15_out, E3, E1);
  and and_16 (and_16_out, E3, E2);
  not not_21 (not_21_out, E2);
  and and_17 (and_17_out, not_21_out, not_22_out);
  not not_22 (not_22_out, E0);
  not not_23 (not_23_out, E2);
  and and_18 (and_18_out, not_23_out, E1);
  and and_19 (and_19_out, E1, not_24_out);
  not not_24 (not_24_out, E0);
  and and_20 (and_20_out, E2, not_25_out, E0);
  not not_25 (not_25_out, E1);
  not not_26 (not_26_out, E2);
  and and_21 (and_21_out, not_26_out, not_27_out);
  not not_27 (not_27_out, E1);
  not not_28 (not_28_out, E3);
  and and_22 (and_22_out, not_28_out, E0);
  not not_29 (not_29_out, E3);
  and and_23 (and_23_out, not_29_out, E2);
  or or_1 (a, and_1_out, and_2_out, and_3_out, E3);
  or or_2 (b, and_4_out, and_5_out, and_6_out, E3);
  or or_3 (c, and_7_out, E1, and_8_out, E3);
  or or_4 (d, and_9_out, and_10_out, and_11_out, and_12_out);
  or or_5 (e, and_13_out, and_14_out, and_15_out, and_16_out);
  or or_6 (f, and_17_out, and_18_out, and_19_out, and_20_out, E3);
  or or_7 (g, and_21_out, and_22_out, and_23_out);
endmodule
